# Fritzing sketch btw_arduino_shield (saved by Fritzing 0.8.4b)

parts:
  Arduino_Pinout = Arduino Prototyping Shield
  R1 = Resistor [tolerance=±5% resistance=220 package=THT]
  LED2 = LED - 5mm [color="Red (633nm)" package="5 mm [THT]"]
  R2 = Resistor [tolerance=±5% resistance=220 package=THT]
  R3 = Resistor [tolerance=±5% resistance=220 package=THT]
  LED3 = LED - 5mm [color="Yellow (595nm)" package="5 mm [THT]"]
  LED4 = LED - 5mm [color="Green (570nm)" package="5 mm [THT]"]
  Q1 = NPN-Transistor [part_number=2n2222a package="TO92 [THT]"]
  Servo_Out = Header 3 [package=molex-1x3_lock]
  R4 = Resistor [tolerance=±5% resistance=350 package=THT]
  R5 = Resistor [tolerance=±5% resistance=350 package=THT]
  D1 = Rectifier Diode [part_number=1N4001 package="300 mil [THT]"]
  Pot_out = Header 3 [package=molex-1x3_lock]
  Motor_out = Header 2 [package=molex-1x2_lock]
  R6 = Resistor [tolerance=±5% resistance=350 package=THT]
  Buttons_UP_DOWN_Out = Header 3 [package=molex-1x3_lock]
  J1 = Basic Servo  # not connected
  M1 = DC Motor  # not connected
  S1 = Pushbutton [package="[THT]"]
  S2 = Pushbutton [package="[THT]"]
  R7 = Rotary Potentiometer (Small) [maximum_resistance=100kΩ package=THT]
  Pot_in = Header 3 [package=molex-1x3_lock]
  LEDs_Out = Header 4 [package=molex-1x4_lock]

nets:
  N1: Arduino_Pinout.D12, R2.Pin_0
  N2: Arduino_Pinout.+5V, Arduino_Pinout.N$75, Arduino_Pinout.N$87, Arduino_Pinout.N$326, Arduino_Pinout.N$327, Arduino_Pinout.N$368, Servo_Out.3, R4.Pin_1, R5.Pin_1, D1.cathode, Pot_out.3, Motor_out.1, Buttons_UP_DOWN_Out.2, Buttons_UP_DOWN_Out.3
  N3: Arduino_Pinout.D11, R3.Pin_0
  N4: Arduino_Pinout.GND, Arduino_Pinout.N$55, Arduino_Pinout.N$81, Arduino_Pinout.N$178, Arduino_Pinout.N$190, Arduino_Pinout.N$323, LED2.cathode, LED3.cathode, LED4.cathode, Q1.E, Servo_Out.1, Pot_out.1, Buttons_UP_DOWN_Out.1, LEDs_Out.1
  N5: Arduino_Pinout.D6, Arduino_Pinout.N$67, Arduino_Pinout.N$74, Servo_Out.2
  N6: Arduino_Pinout.D8, R5.Pin_0
  N7: Arduino_Pinout.D9, R4.Pin_0
  N8: Arduino_Pinout.D13, Arduino_Pinout.N$248, R1.Pin_0
  N9: Arduino_Pinout.D3, R6.Pin_0
  N10: Arduino_Pinout.A1, Arduino_Pinout.N$369, Pot_out.2
  N11: Arduino_Pinout.N$34, R2.Pin_1, LED3.anode, LEDs_Out.3
  N12: Arduino_Pinout.N$41, R3.Pin_1, LED4.anode, LEDs_Out.2
  N13: Arduino_Pinout.N$231, Arduino_Pinout.N$332, R1.Pin_1, LED2.anode, LEDs_Out.4
  N14: Q1.B, R6.Pin_1
  N15: Q1.C, D1.anode, Motor_out.2
  N16: S1.Pin_2, S2.Pin_1, S2.Pin_2
  N17: R7.leg1, Pot_in.3
  N18: R7.wiper, Pot_in.2
  N19: R7.leg2, Pot_in.1

notes:
  Behind The Wire, Prototyping shield schematic to replicate the original BTW circuit, 1.0
  For the first prototyping shield an Adafruit protoshield was used, which is different to this official arduino protoshield.
  This is here to use as a base for the final version which will use this shield and can accurately illustrate how to wire them.
